# Fritzing sketch Sketch (saved by Fritzing 0.9.3b)
breadboards: 1

parts:
  Часть1 = Arduino Uno (Rev3) - ICSP
  LED1 = smd LED [color="Red (633nm)" package="0603 [SMD]"]
  R1 = Resistor [tolerance=±5% resistance=100 package="2010 [SMD]"]
  S1 = Pushbutton [package="[SMD]"]
  R2 = Resistor [tolerance=±5% resistance=10k package="2010 [SMD]"]

nets:
  N1: Часть1.5V, S1.Pin_1, S1.Pin_2
  N2: Часть1.D8, S1.Pin_3, S1.Pin_4, R2.Pin_1
  N3: Часть1.D11_PWM/MOSI, R1.Pin_1
  N4: Часть1.GND, LED1.anode, R2.Pin_0
  N5: LED1.cathode, R1.Pin_0
