# Fritzing sketch Sketch (saved by Fritzing 0.9.3b)
breadboards: 1

parts:
  Часть1 = Arduino Uno (Rev3)
  S1 = Pushbutton [package="[THT]"]
  R1 = Resistor [tolerance=±5% resistance=220 package=THT]
  LED1 = LED - 5mm [color="Red (633nm)" package="5 mm [THT]"]
  R2 = Resistor [tolerance=±5% resistance=220 package=THT]
  R3 = Resistor [tolerance=±5% resistance=220 package=THT]
  LED2 = LED - 5mm [color="Red (633nm)" package="5 mm [THT]"]
  LED3 = LED - 5mm [color="Red (633nm)" package="5 mm [THT]"]
  R4 = Resistor [tolerance=±5% resistance=220 package=THT]

nets:
  N1: Часть1.D8, S1.Pin_3, S1.Pin_4, R1.Pin_1
  N2: Часть1.D9_PWM, R2.Pin_1
  N3: Часть1.D10_PWM/SS, R3.Pin_0
  N4: Часть1.D11_PWM/MOSI, R4.Pin_0
  N5: Часть1.5V, S1.Pin_1, S1.Pin_2
  N6: Часть1.GND, R1.Pin_0, LED1.anode, LED2.anode, LED3.anode
  N7: LED1.cathode, R2.Pin_0
  N8: R3.Pin_1, LED2.cathode
  N9: LED3.cathode, R4.Pin_1

// code stored in the sketch: Untitled2.ino
int ledPin[3] = {9, 10, 11};
int switchPin = 8;
boolean lastButton = LOW;
boolean currentButton = LOW;
boolean ledOn = true;
int ledLevel = 0;
int i = 0;

void setup() {
  // put your setup code here, to run once:
  Serial.begin(9600);
  pinMode(switchPin, INPUT);
  
  for (int i = 0; i < 3; ++i)
    pinMode(ledPin[i], OUTPUT);
}

boolean debounce(boolean last)
{
  boolean current = digitalRead(switchPin);
  if (last != current)
  {
    delay(5);
    current = digitalRead(switchPin);
  }
  return current;
}

void ledLight(int i){
  ledLevel += 1;
  if (ledLevel > 255){
      ledLevel = 0;
    }
  delay(10);
  analogWrite(ledPin[i], ledLevel);
}

void loop() {
  // put your main code here, to run repeatedly:
//First programm
  Serial.println(currentButton);
  currentButton = debounce(lastButton);
  if (currentButton == HIGH && lastButton == LOW){
    ledLevel = 0;
    analogWrite(ledPin[i], ledLevel);
    ++i;
    if (i > 2) i = 0;
  }
  lastButton = currentButton;
  ledLight(i);
}
