# Fritzing sketch Sketch (saved by Fritzing 0.9.3b)
breadboards: 1

parts:
  Часть1 = Arduino Uno (Rev3)
  R1 = Resistor [tolerance=±5% resistance=220 package="2010 [SMD]"]
  LED1 = smd LED [color="Red (633nm)" package="0603 [SMD]"]
  RE1 = Rotary Encoder [package=THT]

nets:
  N1: Часть1.A5/SCL, RE1.EncoderPinC
  N2: Часть1.D5_PWM, R1.Pin_0
  N3: Часть1.5V, RE1.EncoderPinA
  N4: Часть1.GND, LED1.anode, RE1.EncoderPinB
  N5: R1.Pin_1, LED1.cathode
